// Logisim project Flip_FLop_D.circ as structural Verilog: 1 circuit, main circuit main
module main (
  input  X,
  output Q,
  output Q_prime
);

  wire AND_2_out, AND_out, CLOCK_out, INVERTER_out;

  Clock CLOCK (.out(CLOCK_out));
  not INVERTER (INVERTER_out, X);
  and AND (AND_out, X, CLOCK_out);
  and AND_2 (AND_2_out, CLOCK_out, INVERTER_out);
  nor NOR (Q, AND_out, Q_prime);
  nor NOR_2 (Q_prime, Q, AND_2_out);

  // Notes on the sheet:
  //   D_FLIP_FLOP
endmodule
