// Logisim project Flip_Flop_SR.circ as structural Verilog: 1 circuit, main circuit main
module main (
  input  S,
  input  R,
  output Q,
  output Q_prime
);

  wire CLOCK_out, NAND_2_out, NAND_out;

  Clock CLOCK (.out(CLOCK_out));
  nand NAND (NAND_out, S, CLOCK_out);
  nand NAND_2 (NAND_2_out, CLOCK_out, R);
  nand NAND_3 (Q, NAND_out, Q_prime);
  nand NAND_4 (Q_prime, Q, NAND_2_out);
endmodule
