// Logisim project Multiplexer_2X1.circ as structural Verilog: 1 circuit, main circuit main
module main (
  input  X,
  input  Y,
  input  SEL,
  output OUT
);

  wire AND_2_out, AND_out, NOT_out;

  not NOT (NOT_out, SEL);
  and AND (AND_out, X, NOT_out);
  and AND_2 (AND_2_out, Y, SEL);
  or OR (OUT, AND_out, AND_2_out);

  // Notes on the sheet:
  //   2:1 MUX
endmodule
