// Logisim project Switching_two_leds.circ as structural Verilog: 1 circuit, main circuit main
module main (
);

  wire button_2_out, Button_out, j_k_ff_1_q, j_k_ff_1_qn, NAND_2_out, NAND_3_out, NAND_4_out, NAND_5_out,
       NAND_6_out, NAND_7_out, NAND_8_out, NAND_out, not_1_out;

  Button Button (.out(Button_out));
  Button button_2 (.out(button_2_out));
  nand NAND (NAND_out, NAND_8_out, 1'b1, Button_out);
  nand NAND_2 (NAND_2_out, Button_out, 1'b1, NAND_7_out);
  not not_1 (not_1_out, Button_out);
  J_K_Flip_Flop j_k_ff_1 (
    .J(1'b1), .clk(button_2_out), .K(1'b1), .Q(j_k_ff_1_q), .Qn(j_k_ff_1_qn));  // open: preset, en, reset
  LED led_1 (.in(j_k_ff_1_q));
  LED led_2 (.in(j_k_ff_1_qn));
  nand NAND_3 (NAND_3_out, NAND_out, NAND_4_out);
  nand NAND_4 (NAND_4_out, NAND_3_out, NAND_2_out);
  nand NAND_5 (NAND_5_out, NAND_3_out, not_1_out);
  nand NAND_6 (NAND_6_out, not_1_out, NAND_4_out);
  nand NAND_7 (NAND_7_out, NAND_5_out, NAND_8_out);
  nand NAND_8 (NAND_8_out, NAND_7_out, NAND_6_out);
  LED LED_1_dup2 (.in(NAND_7_out));
  LED LED_2_dup2 (.in(NAND_8_out));

  // Notes on the sheet:
  //   Switching two Leds using JK Flip Flop
endmodule
