// Logisim project E1to6.circ as structural Verilog: 6 circuits, main circuit E1
module E1 (
  input  A,
  input  B,
  output C
);

  wire nand_1_out, nand_2_out, nand_3_out;

  nand nand_1 (nand_1_out, A, B);
  nand nand_2 (nand_2_out, A, nand_1_out);
  nand nand_3 (nand_3_out, nand_1_out, B);
  nand nand_4 (C, nand_2_out, nand_3_out);

  // Notes on the sheet:
  //   XOR gate using NAND gates
endmodule

module E2 (
  input  A,
  input  B,
  output C
);

  wire nor_1_out, nor_2_out, nor_3_out;

  nor nor_1 (nor_1_out, A, nor_2_out);
  nor nor_2 (nor_2_out, A, B);
  nor nor_3 (nor_3_out, nor_2_out, B);
  nor nor_4 (C, nor_1_out, nor_3_out);

  // Notes on the sheet:
  //   XOR gate using NOR gates
endmodule

module E3 (
  input  A,
  input  B,
  input  C,
  output D
);

  wire and_1_out;

  and and_1 (and_1_out, A, B);
  and and_2 (D, and_1_out, C);

  // Notes on the sheet:
  //   AND with 3 inputs
endmodule

module E4 (
  input  A,
  input  B,
  input  C,
  input  D,
  output E
);

  wire or_1_out, or_2_out;

  or or_1 (or_1_out, A, B);
  or or_2 (or_2_out, C, D);
  or or_3 (E, or_1_out, or_2_out);

  // Notes on the sheet:
  //   OR gate with 4 inputs
endmodule

module E5 (
  input  A,
  input  B,
  output E
);

  nand nand_1 (E, A, B);

  // Notes on the sheet:
  //   NOT gate with 2 inputs using NAND gate
endmodule

module E6 (
  input  A,
  input  B,
  output E
);

  wire nor_1_out, nor_2_out;

  nor nor_1 (nor_1_out, A, A);
  nor nor_2 (nor_2_out, B, B);
  nor nor_3 (E, nor_1_out, nor_2_out);

  // Notes on the sheet:
  //   AND gate using NOR gates
endmodule
