// Logisim project H2_4-bit-decoder.circ as structural Verilog: 1 circuit, main circuit main
module main (
  input  in_1,
  input  in_2,
  input  in_3,
  input  in_4
);

  wire and_1_out, and_2_out, and_3_out, and_4_out, and_5_out, and_6_out, and_7_out, and_8_out, and_9_out,
       and_10_out, and_11_out, and_12_out, and_13_out, and_14_out, and_15_out, and_16_out, not_1_out,
       not_2_out, not_3_out, not_4_out, not_5_out, not_6_out, not_7_out, not_8_out;

  and and_1 (and_1_out, not_1_out, not_5_out, not_3_out, not_4_out);
  LED _0 (.in(and_1_out));
  and and_2 (and_2_out, not_1_out, not_5_out, not_3_out, not_7_out);
  LED _1 (.in(and_2_out));
  and and_3 (and_3_out, not_1_out, not_5_out, not_7_out, not_6_out);
  and and_4 (and_4_out, not_1_out, not_5_out, not_6_out, not_4_out);
  LED _3 (.in(and_3_out));
  LED _2 (.in(and_4_out));
  and and_5 (and_5_out, not_1_out, not_3_out, not_4_out, not_8_out);
  LED _4 (.in(and_5_out));
  and and_6 (and_6_out, not_1_out, not_3_out, not_7_out, not_8_out);
  LED _5 (.in(and_6_out));
  not not_1 (not_1_out, in_1);
  not not_2 (not_2_out, not_1_out);
  and and_7 (and_7_out, not_1_out, not_4_out, not_6_out, not_8_out);
  and and_8 (and_8_out, not_7_out, not_1_out, not_6_out, not_8_out);
  LED _6 (.in(and_7_out));
  LED _7 (.in(and_8_out));
  not not_3 (not_3_out, in_3);
  not not_4 (not_4_out, in_4);
  not not_5 (not_5_out, in_2);
  not not_6 (not_6_out, not_3_out);
  not not_7 (not_7_out, not_4_out);
  not not_8 (not_8_out, not_5_out);
  and and_9 (and_9_out, not_2_out, not_4_out, not_3_out, not_5_out);
  LED _8 (.in(and_9_out));
  and and_10 (and_10_out, not_5_out, not_3_out, not_7_out, not_2_out);
  LED _9 (.in(and_10_out));
  and and_11 (and_11_out, not_5_out, not_4_out, not_6_out, not_2_out);
  LED _10 (.in(and_11_out));
  and and_12 (and_12_out, not_5_out, not_7_out, not_6_out, not_2_out);
  and and_13 (and_13_out, not_3_out, not_4_out, not_8_out, not_2_out);
  LED _11 (.in(and_12_out));
  LED _12 (.in(and_13_out));
  and and_14 (and_14_out, not_7_out, not_3_out, not_8_out, not_2_out);
  LED _13 (.in(and_14_out));
  and and_15 (and_15_out, not_4_out, not_6_out, not_8_out, not_2_out);
  LED _14 (.in(and_15_out));
  and and_16 (and_16_out, not_2_out, not_8_out, not_6_out, not_7_out);
  LED _15 (.in(and_16_out));

  // Notes on the sheet:
  //   4 BIT DECODER
endmodule
