// Logisim project H3_4-bit-encoder.circ as structural Verilog: 1 circuit, main circuit main
module main (
  input  D3,
  input  D2,
  input  D1,
  input  D0,
  output A0,
  output A1,
  output V
);

  wire and_1_out, not_1_out;

  not not_1 (not_1_out, D2);
  or or_1 (A0, D3, and_1_out);
  and and_1 (and_1_out, not_1_out, D1);
  or or_2 (A1, D2, D3);
  ExactlyOne xor_1 (.out(V), .in0(D3), .in1(D2), .in2(D1), .in3(D0));

  // Notes on the sheet:
  //   4 BIT ENCODER
endmodule
