// Logisim project H4_8-bit-full-adder.circ as structural Verilog: 3 circuits, main circuit 1_bit_adder
module _1_bit_adder (
  input  Cin,
  input  A,
  input  B,
  output Sum,
  output Cout
);

  wire and_1_out, and_2_out, xor_1_out;

  xor xor_1 (xor_1_out, A, B);
  xor xor_2 (Sum, xor_1_out, Cin);
  and and_1 (and_1_out, Cin, xor_1_out);
  and and_2 (and_2_out, B, A);
  or or_1 (Cout, and_1_out, and_2_out);
endmodule

module _4_bit_adder (
  input  Cin,
  input  [3:0] A4,
  input  [3:0] B4,
  output [3:0] Sum,
  output Cout
);

  wire n1_bit_adder_1_cout, n1_bit_adder_2_cout, n1_bit_adder_3_cout;

  _1_bit_adder u_1_bit_adder_1 (.Cin(Cin), .A(A4[0]), .B(B4[0]), .Sum(Sum[0]), .Cout(n1_bit_adder_1_cout));
  _1_bit_adder u_1_bit_adder_2 (
    .Cin(n1_bit_adder_1_cout), .A(A4[1]), .B(B4[1]), .Sum(Sum[1]), .Cout(n1_bit_adder_2_cout));
  _1_bit_adder u_1_bit_adder_3 (
    .Cin(n1_bit_adder_2_cout), .A(A4[2]), .B(B4[2]), .Sum(Sum[2]), .Cout(n1_bit_adder_3_cout));
  _1_bit_adder u_1_bit_adder_4 (.Cin(n1_bit_adder_3_cout), .A(A4[3]), .B(B4[3]), .Sum(Sum[3]), .Cout(Cout));
endmodule

module _8_bit_adder (
  input  Cin,
  input  [7:0] A,
  input  [7:0] B,
  output [7:0] Sum,
  output Cout
);

  wire n4_bit_adder_1_cout;

  _4_bit_adder u_4_bit_adder_1 (.Cin(Cin), .A4(A[3:0]), .B4(B[3:0]), .Sum(Sum[3:0]), .Cout(n4_bit_adder_1_cout));
  _4_bit_adder u_4_bit_adder_2 (.Cin(n4_bit_adder_1_cout), .A4(A[7:4]), .B4(B[7:4]), .Sum(Sum[7:4]), .Cout(Cout));
endmodule
