// Logisim project H5_8-bit-multiplier.circ as structural Verilog: 4 circuits, main circuit FA
module FA (
  input  Cin,
  input  A,
  input  B,
  output Sum,
  output Cout
);

  wire and_1_out, and_2_out, xor_1_out;

  xor xor_1 (xor_1_out, A, B);
  xor xor_2 (Sum, xor_1_out, Cin);
  and and_1 (and_1_out, Cin, xor_1_out);
  and and_2 (and_2_out, B, A);
  or or_1 (Cout, and_1_out, and_2_out);
endmodule

// 8 Bit Adder
module _8bit_FA (
  input  A0,
  input  A1,
  input  A2,
  input  A3,
  input  A4,
  input  A5,
  input  A6,
  input  A7,
  input  [7:0] B,
  output S0,
  output S1,
  output S2,
  output S3,
  output S4,
  output S5,
  output S6,
  output S7,
  output Cout
);

  wire adder_1_cout, fa_1_cout, fa_2_cout, fa_3_cout, fa_4_cout, fa_5_cout, fa_6_cout;

  Adder #(.width(1)) adder_1 (.a(A0), .b(B[0]), .out(S0), .cout(adder_1_cout));  // open: cin
  FA fa_1 (.Cin(adder_1_cout), .A(A1), .B(B[1]), .Sum(S1), .Cout(fa_1_cout));
  FA fa_2 (.Cin(fa_1_cout), .A(A2), .B(B[2]), .Sum(S2), .Cout(fa_2_cout));
  FA fa_3 (.Cin(fa_2_cout), .A(A3), .B(B[3]), .Sum(S3), .Cout(fa_3_cout));
  FA fa_4 (.Cin(fa_3_cout), .A(A4), .B(B[4]), .Sum(S4), .Cout(fa_4_cout));
  FA fa_5 (.Cin(fa_4_cout), .A(A5), .B(B[5]), .Sum(S5), .Cout(fa_5_cout));
  FA fa_6 (.Cin(fa_5_cout), .A(A6), .B(B[6]), .Sum(S6), .Cout(fa_6_cout));
  FA fa_7 (.Cin(fa_6_cout), .A(A7), .B(A7), .Sum(S7), .Cout(Cout));

  assign B[7] = A7;
endmodule

module _8bit_Multiplier (
  input  A0,
  input  A1,
  input  A2,
  input  A3,
  input  in_5,
  input  A4,
  input  A5,
  input  A6,
  input  A7,
  input  A0_2,
  input  A0_3,
  input  A0_4,
  input  A0_5,
  input  A0_6,
  input  A0_7,
  input  A0_8,
  input  A1_2,
  input  A1_3,
  input  A1_4,
  input  A1_5,
  input  A1_6,
  input  A1_7,
  input  A1_8,
  input  A2_2,
  input  A2_3,
  input  A2_4,
  input  A2_5,
  input  A2_6,
  input  A2_7,
  input  A2_8,
  input  A3_2,
  input  A3_3,
  input  A3_4,
  input  A3_5,
  input  A3_6,
  input  A3_7,
  input  A3_8,
  input  A4_2,
  input  A4_3,
  input  A4_4,
  input  A4_5,
  input  A4_6,
  input  A4_7,
  input  A4_8,
  input  A5_2,
  input  A5_3,
  input  A5_4,
  input  A5_5,
  input  A5_6,
  input  A5_7,
  input  A5_8,
  input  A6_2,
  input  A6_3,
  input  A6_4,
  input  A6_5,
  input  A6_6,
  input  A6_7,
  input  A6_8,
  input  A7_2,
  input  A7_3,
  input  A7_4,
  input  A7_5,
  input  A7_6,
  input  A7_7,
  input  A7_8,
  input  B0,
  input  B1,
  input  B2,
  input  B3,
  input  B4,
  input  B5,
  input  B6,
  input  B7,
  output [15:0] P
);

  wire and_2_out, and_3_out, and_4_out, and_5_out, and_6_out, and_7_out, and_8_out, n8bit_fa_1_cout,
       n8bit_fa_1_s1, n8bit_fa_1_s2, n8bit_fa_1_s3, n8bit_fa_1_s4, n8bit_fa_1_s5, n8bit_fa_1_s6,
       n8bit_fa_1_s7, n8bit_fa_2_cout, n8bit_fa_2_s1, n8bit_fa_2_s2, n8bit_fa_2_s3, n8bit_fa_2_s4,
       n8bit_fa_2_s5, n8bit_fa_2_s6, n8bit_fa_2_s7, n8bit_fa_3_cout, n8bit_fa_3_s1, n8bit_fa_3_s2,
       n8bit_fa_3_s3, n8bit_fa_3_s4, n8bit_fa_3_s5, n8bit_fa_3_s6, n8bit_fa_3_s7, n8bit_fa_4_cout,
       n8bit_fa_4_s1, n8bit_fa_4_s2, n8bit_fa_4_s3, n8bit_fa_4_s4, n8bit_fa_4_s5, n8bit_fa_4_s6,
       n8bit_fa_4_s7, n8bit_fa_5_cout, n8bit_fa_5_s1, n8bit_fa_5_s2, n8bit_fa_5_s3, n8bit_fa_5_s4,
       n8bit_fa_5_s5, n8bit_fa_5_s6, n8bit_fa_5_s7, n8bit_fa_6_cout, n8bit_fa_6_s1, n8bit_fa_6_s2,
       n8bit_fa_6_s3, n8bit_fa_6_s4, n8bit_fa_6_s5, n8bit_fa_6_s6, n8bit_fa_6_s7;
  wire [7:0] and_9_out, and_17_out, and_25_out, and_33_out, and_41_out, and_49_out, and_57_out;

  and and_1 (P[0], A0, B0);
  and and_2 (and_2_out, A1, B0);
  and and_3 (and_3_out, A2, B0);
  and and_4 (and_4_out, A3, B0);
  and and_5 (and_5_out, A4, B0);
  and and_6 (and_6_out, A5, B0);
  and and_7 (and_7_out, A6, B0);
  and and_8 (and_8_out, A7, B0);
  and and_9 (and_9_out[0], A0_2, B1);
  and and_10 (and_9_out[1], A1_2, B1);
  and and_11 (and_9_out[2], A2_2, B1);
  and and_12 (and_9_out[3], A3_2, B1);
  and and_13 (and_9_out[4], A4_2, B1);
  and and_14 (and_9_out[5], A5_2, B1);
  and and_15 (and_9_out[6], A6_2, B1);
  and and_16 (and_9_out[7], A7_2, B1);
  _8bit_FA u_8bit_fa_1 (
    .A0(and_2_out), .A1(and_3_out), .A2(and_4_out), .A3(and_5_out), .A4(and_6_out), .A5(and_7_out),
    .A6(and_8_out), .A7(in_5), .B(and_9_out), .S0(P[1]), .S1(n8bit_fa_1_s1), .S2(n8bit_fa_1_s2),
    .S3(n8bit_fa_1_s3), .S4(n8bit_fa_1_s4), .S5(n8bit_fa_1_s5), .S6(n8bit_fa_1_s6), .S7(n8bit_fa_1_s7),
    .Cout(n8bit_fa_1_cout));
  and and_17 (and_17_out[0], A0_3, B2);
  and and_18 (and_17_out[1], A1_3, B2);
  and and_19 (and_17_out[2], A2_3, B2);
  and and_20 (and_17_out[3], A3_3, B2);
  and and_21 (and_17_out[4], A4_3, B2);
  and and_22 (and_17_out[5], A5_3, B2);
  and and_23 (and_17_out[6], A6_3, B2);
  and and_24 (and_17_out[7], A7_3, B2);
  _8bit_FA u_8bit_fa_2 (
    .A0(n8bit_fa_1_s1), .A1(n8bit_fa_1_s2), .A2(n8bit_fa_1_s3), .A3(n8bit_fa_1_s4), .A4(n8bit_fa_1_s5),
    .A5(n8bit_fa_1_s6), .A6(n8bit_fa_1_s7), .A7(n8bit_fa_1_cout), .B(and_17_out), .S0(P[2]),
    .S1(n8bit_fa_2_s1), .S2(n8bit_fa_2_s2), .S3(n8bit_fa_2_s3), .S4(n8bit_fa_2_s4), .S5(n8bit_fa_2_s5),
    .S6(n8bit_fa_2_s6), .S7(n8bit_fa_2_s7), .Cout(n8bit_fa_2_cout));
  and and_25 (and_25_out[0], A0_4, B3);
  and and_26 (and_25_out[1], A1_4, B3);
  and and_27 (and_25_out[2], A2_4, B3);
  and and_28 (and_25_out[3], A3_4, B3);
  and and_29 (and_25_out[4], A4_4, B3);
  and and_30 (and_25_out[5], A5_4, B3);
  and and_31 (and_25_out[6], A6_4, B3);
  and and_32 (and_25_out[7], A7_4, B3);
  _8bit_FA u_8bit_fa_3 (
    .A0(n8bit_fa_2_s1), .A1(n8bit_fa_2_s2), .A2(n8bit_fa_2_s3), .A3(n8bit_fa_2_s4), .A4(n8bit_fa_2_s5),
    .A5(n8bit_fa_2_s6), .A6(n8bit_fa_2_s7), .A7(n8bit_fa_2_cout), .B(and_25_out), .S0(P[3]),
    .S1(n8bit_fa_3_s1), .S2(n8bit_fa_3_s2), .S3(n8bit_fa_3_s3), .S4(n8bit_fa_3_s4), .S5(n8bit_fa_3_s5),
    .S6(n8bit_fa_3_s6), .S7(n8bit_fa_3_s7), .Cout(n8bit_fa_3_cout));
  and and_33 (and_33_out[0], A0_5, B4);
  and and_34 (and_33_out[1], A1_5, B4);
  and and_35 (and_33_out[2], A2_5, B4);
  and and_36 (and_33_out[3], A3_5, B4);
  and and_37 (and_33_out[4], A4_5, B4);
  and and_38 (and_33_out[5], A5_5, B4);
  and and_39 (and_33_out[6], A6_5, B4);
  and and_40 (and_33_out[7], A7_5, B4);
  _8bit_FA u_8bit_fa_4 (
    .A0(n8bit_fa_3_s1), .A1(n8bit_fa_3_s2), .A2(n8bit_fa_3_s3), .A3(n8bit_fa_3_s4), .A4(n8bit_fa_3_s5),
    .A5(n8bit_fa_3_s6), .A6(n8bit_fa_3_s7), .A7(n8bit_fa_3_cout), .B(and_33_out), .S0(P[4]),
    .S1(n8bit_fa_4_s1), .S2(n8bit_fa_4_s2), .S3(n8bit_fa_4_s3), .S4(n8bit_fa_4_s4), .S5(n8bit_fa_4_s5),
    .S6(n8bit_fa_4_s6), .S7(n8bit_fa_4_s7), .Cout(n8bit_fa_4_cout));
  and and_41 (and_41_out[0], A0_6, B5);
  and and_42 (and_41_out[1], A1_6, B5);
  and and_43 (and_41_out[2], A2_6, B5);
  and and_44 (and_41_out[3], A3_6, B5);
  and and_45 (and_41_out[4], A4_6, B5);
  and and_46 (and_41_out[5], A5_6, B5);
  and and_47 (and_41_out[6], A6_6, B5);
  and and_48 (and_41_out[7], A7_6, B5);
  _8bit_FA u_8bit_fa_5 (
    .A0(n8bit_fa_4_s1), .A1(n8bit_fa_4_s2), .A2(n8bit_fa_4_s3), .A3(n8bit_fa_4_s4), .A4(n8bit_fa_4_s5),
    .A5(n8bit_fa_4_s6), .A6(n8bit_fa_4_s7), .A7(n8bit_fa_4_cout), .B(and_41_out), .S0(P[5]),
    .S1(n8bit_fa_5_s1), .S2(n8bit_fa_5_s2), .S3(n8bit_fa_5_s3), .S4(n8bit_fa_5_s4), .S5(n8bit_fa_5_s5),
    .S6(n8bit_fa_5_s6), .S7(n8bit_fa_5_s7), .Cout(n8bit_fa_5_cout));
  and and_49 (and_49_out[0], A0_7, B6);
  and and_50 (and_49_out[1], A1_7, B6);
  and and_51 (and_49_out[2], A2_7, B6);
  and and_52 (and_49_out[3], A3_7, B6);
  and and_53 (and_49_out[4], A4_7, B6);
  and and_54 (and_49_out[5], A5_7, B6);
  and and_55 (and_49_out[6], A6_7, B6);
  and and_56 (and_49_out[7], A7_7, B6);
  _8bit_FA u_8bit_fa_6 (
    .A0(n8bit_fa_5_s1), .A1(n8bit_fa_5_s2), .A2(n8bit_fa_5_s3), .A3(n8bit_fa_5_s4), .A4(n8bit_fa_5_s5),
    .A5(n8bit_fa_5_s6), .A6(n8bit_fa_5_s7), .A7(n8bit_fa_5_cout), .B(and_49_out), .S0(P[6]),
    .S1(n8bit_fa_6_s1), .S2(n8bit_fa_6_s2), .S3(n8bit_fa_6_s3), .S4(n8bit_fa_6_s4), .S5(n8bit_fa_6_s5),
    .S6(n8bit_fa_6_s6), .S7(n8bit_fa_6_s7), .Cout(n8bit_fa_6_cout));
  _8bit_FA u_8bit_fa_7 (
    .A0(n8bit_fa_6_s1), .A1(n8bit_fa_6_s2), .A2(n8bit_fa_6_s3), .A3(n8bit_fa_6_s4), .A4(n8bit_fa_6_s5),
    .A5(n8bit_fa_6_s6), .A6(n8bit_fa_6_s7), .A7(n8bit_fa_6_cout), .B(and_57_out), .S0(P[7]), .S1(P[8]),
    .S2(P[9]), .S3(P[10]), .S4(P[11]), .S5(P[12]), .S6(P[13]), .S7(P[14]), .Cout(P[15]));
  and and_57 (and_57_out[0], A0_8, B7);
  and and_58 (and_57_out[1], A1_8, B7);
  and and_59 (and_57_out[2], A2_8, B7);
  and and_60 (and_57_out[3], A3_8, B7);
  and and_61 (and_57_out[4], A4_8, B7);
  and and_62 (and_57_out[5], A5_8, B7);
  and and_63 (and_57_out[6], A6_8, B7);
  and and_64 (and_57_out[7], A7_8, B7);
endmodule

module circuit (
  input  [7:0] in_1,
  input  in_2,
  input  [7:0] in_3,
  output [15:0] P
);

  wire [6:0] and_10_out;
  wire [7:0] adder_5_out, and_1_out, undriven, undriven_2, undriven_3, undriven_4, undriven_5, undriven_6;
  wire [7:1] adder_1_out, adder_2_out, adder_3_out, adder_4_out, adder_6_out;
  wire [7:7] adder_1_cout, adder_2_cout, adder_3_cout, adder_4_cout, adder_6_cout;

  and and_1 (and_1_out[0], in_1[0], in_3[1]);
  and and_2 (and_1_out[1], in_1[1], in_3[1]);
  and and_3 (and_1_out[2], in_1[2], in_3[1]);
  and and_4 (and_1_out[3], in_1[3], in_3[1]);
  and and_5 (and_1_out[4], in_1[4], in_3[1]);
  and and_6 (and_1_out[5], in_1[5], in_3[1]);
  and and_7 (and_1_out[6], in_1[6], in_3[1]);
  and and_8 (and_1_out[7], in_1[7], in_3[1]);
  and and_9 (P[0], in_1[0], in_3[0]);
  and and_10 (and_10_out[0], in_1[1], in_3[0]);
  and and_11 (and_10_out[1], in_1[2], in_3[0]);
  and and_12 (and_10_out[2], in_1[3], in_3[0]);
  and and_13 (and_10_out[3], in_1[4], in_3[0]);
  and and_14 (and_10_out[4], in_1[5], in_3[0]);
  and and_15 (and_10_out[5], in_1[6], in_3[0]);
  and and_16 (and_10_out[6], in_1[7], in_3[0]);
  Adder adder_1 (
    .a({in_2, and_10_out}), .b(and_1_out), .out({adder_1_out, P[1]}), .cout(adder_1_cout[7]));  // open: cin
  Adder adder_2 (
    .a({adder_1_cout[7], adder_1_out}), .b(undriven), .out({adder_2_out, P[2]}), .cout(adder_2_cout[7]));  // open: cin
  Adder adder_3 (
    .a({adder_2_cout[7], adder_2_out}), .b(undriven_2), .out({adder_3_out, P[3]}), .cout(adder_3_cout[7]));  // open: cin
  Adder adder_4 (
    .a({adder_3_cout[7], adder_3_out}), .b(undriven_3), .out({adder_4_out, P[4]}), .cout(adder_4_cout[7]));  // open: cin
  Adder adder_5 (
    .a({adder_4_cout[7], adder_4_out}), .b(undriven_4), .out({adder_5_out[6:0], P[5]}), .cout(adder_5_out[7]));  // open: cin
  Adder adder_6 (.a(adder_5_out), .b(undriven_5), .out({adder_6_out, P[6]}), .cout(adder_6_cout[7]));  // open: cin
  Adder adder_7 (.a({adder_6_cout[7], adder_6_out}), .b(undriven_6), .out(P[14:7]), .cout(P[15]));  // open: cin
endmodule
