// Logisim project M10_4bit-shifter-&-rotator.circ as structural Verilog: 1 circuit, main circuit main
module main (
  input  A0,
  input  A1,
  input  A2,
  input  A3,
  input  in_5,
  input  in_6,
  input  [1:0] S1S2,
  output B3,
  output B2,
  output B1,
  output B0
);

  Multiplexer #(.select(2), .enable("false")) multiplexer_1 (
    .in0(A2), .in1(in_5), .in2(A2), .in3(A0), .out(B3), .sel(S1S2));
  Multiplexer #(.select(2), .enable("false")) multiplexer_2 (
    .in0(A1), .in1(A3), .in2(A1), .in3(A3), .out(B2), .sel(S1S2));
  Multiplexer #(.select(2), .enable("false")) multiplexer_3 (
    .in0(A0), .in1(A2), .in2(A0), .in3(A2), .out(B1), .sel(S1S2));
  Multiplexer #(.select(2), .enable("false")) multiplexer_4 (
    .in0(in_6), .in1(A1), .in2(A3), .in3(A1), .out(B0), .sel(S1S2));

  // Notes on the sheet:
  //   4 bit universal shifter/rotator
endmodule
