// Logisim project M11_4-bit-negator.circ as structural Verilog: 1 circuit, main circuit main
module main (
  input  [3:0] A,
  output [3:0] minus_A
);

  Negator #(.width(4)) negator_1 (.in(A), .out(minus_A));

  // Notes on the sheet:
  //   4 bit negator
endmodule
