// Logisim project M12_4-bit-to-2's-complement.circ as structural Verilog: 1 circuit, main circuit main
module main (
  input  in_1,
  input  in_2,
  input  in_3,
  input  in_4,
  input  in_5,
  output out_6,
  output out_7,
  output out_8,
  output out_9
);

  wire and_1_out, and_2_out, and_3_out, not_1_out, not_2_out, not_3_out, not_4_out;

  not not_1 (not_1_out, in_2);
  not not_2 (not_2_out, in_3);
  not not_3 (not_3_out, in_4);
  not not_4 (not_4_out, in_5);
  and and_1 (and_1_out, in_1, not_1_out);
  and and_2 (and_2_out, and_1_out, not_2_out);
  xor xor_1 (out_6, in_1, not_1_out);
  xor xor_2 (out_7, and_1_out, not_2_out);
  xor xor_3 (out_8, and_2_out, not_3_out);
  and and_3 (and_3_out, and_2_out, not_3_out);
  xor xor_4 (out_9, and_3_out, not_4_out);

  // Notes on the sheet:
  //   4 bit to 2's complement
endmodule
