// Logisim project M15_4-bit-from-decimal.circ as structural Verilog: 1 circuit, main circuit main
module main (
  input  _1,
  input  _2,
  input  _3,
  input  _4,
  input  _5,
  input  _6,
  input  _7,
  input  _8,
  input  _9,
  output A0,
  output A1,
  output A2,
  output A3
);

  or or_1 (A0, _1, _3, _4, _7, _9);
  or or_2 (A1, _3, _2, _6, _7);
  or or_3 (A2, _4, _5, _6, _7);
  or or_4 (A3, _8, _9);

  // Notes on the sheet:
  //   Decimal to binar
endmodule
