// Logisim project M1_8-bit-comparator.circ as structural Verilog: 1 circuit, main circuit main
module main (
  input  [7:0] A,
  input  [7:0] B,
  output A___B,
  output A___B_2,
  output A___B_3
);

  Comparator comparator_1 (.a(A), .b(B), .gt(A___B), .eq(A___B_2), .lt(A___B_3));

  // Notes on the sheet:
  //   8 bit comparator
endmodule
