// Logisim project M2_3-bit-decoder.circ as structural Verilog: 1 circuit, main circuit main
module main (
  input  [2:0] Num
);

  wire decoder_1_out0, decoder_1_out1, decoder_1_out2, decoder_1_out3, decoder_1_out4, decoder_1_out5,
       decoder_1_out6, decoder_1_out7;

  Decoder #(.select(3), .enable("false")) decoder_1 (
    .out0(decoder_1_out0), .out1(decoder_1_out1), .out2(decoder_1_out2), .out3(decoder_1_out3),
    .out4(decoder_1_out4), .out5(decoder_1_out5), .out6(decoder_1_out6), .out7(decoder_1_out7), .sel(Num));
  LED _0 (.in(decoder_1_out0));
  LED _1 (.in(decoder_1_out1));
  LED _2 (.in(decoder_1_out2));
  LED _3 (.in(decoder_1_out3));
  LED _4 (.in(decoder_1_out4));
  LED _5 (.in(decoder_1_out5));
  LED _6 (.in(decoder_1_out6));
  LED _7 (.in(decoder_1_out7));

  // Notes on the sheet:
  //   3 to 8 decoder
endmodule
