// Logisim project M3_8-bit-encoder.circ as structural Verilog: 1 circuit, main circuit main
module main (
  input  A0,
  input  A1,
  input  A2,
  input  A3,
  input  A4,
  input  A5,
  input  A6,
  input  A7,
  output [2:0] B,
  output out_10
);

  Priority_Encoder priority_encoder_1 (
    .in0(A0), .in1(A1), .in2(A2), .in3(A3), .in4(A4), .in5(A5), .in6(A6), .in7(A7), .out(B), .gs(out_10));  // open: en_in, en_out

  // Notes on the sheet:
  //   8 bit encoder
endmodule
