// Logisim project M4_16-bit-adder.circ as structural Verilog: 1 circuit, main circuit main
module main (
  input  [15:0] A,
  input  [15:0] B,
  output [15:0] Sum,
  output Cout
);

  Adder #(.width(16)) adder_1 (.a(A), .b(B), .out(Sum), .cout(Cout));  // open: cin

  // Notes on the sheet:
  //   16 bit full adder
endmodule
