// Logisim project M5_4-bit-multiplier.circ as structural Verilog: 1 circuit, main circuit main
module main (
  input  [3:0] A,
  input  [3:0] B,
  output [3:0] P,
  output [3:0] Cout
);

  Multiplier #(.width(4)) multiplier_1 (.a(A), .b(B), .out(P), .cout(Cout));  // open: cin

  // Notes on the sheet:
  //   4 bit multiplier
endmodule
