// Logisim project M6_4-bit-subtractor.circ as structural Verilog: 1 circuit, main circuit main
module main (
  input  [3:0] A,
  input  [3:0] B,
  output [3:0] C,
  output Cout
);

  Subtractor #(.width(4)) subtractor_1 (.a(A), .b(B), .out(C), .bout(Cout));  // open: bin

  // Notes on the sheet:
  //   4 bit subtractor
endmodule
