// Logisim project M9_4-bit-devider.circ as structural Verilog: 1 circuit, main circuit main
module main (
  input  [3:0] A,
  input  [3:0] B,
  output [3:0] Q,
  output [3:0] R
);

  Divider #(.width(4)) divider_1 (.a(A), .b(B), .out(Q), .rem(R));  // open: upper

  // Notes on the sheet:
  //   4 bit divider
endmodule
